// Logisim project AND gate 3-bit input slow.circ as structural Verilog: 1 circuit, main circuit main
module main (
  input  input0,
  input  input1,
  input  input2,
  output output0
);

  wire transistor_1_out, transistor_3_out, transistor_6_out, transistor_7_out, transistor_10_out;

  Transistor transistor_1 (.in(1'b1), .out(transistor_1_out), .gate(input1));
  Transistor transistor_2 (.in(1'b1), .out(transistor_1_out), .gate(input0));
  Transistor transistor_3 (.in(1'b1), .out(transistor_3_out), .gate(transistor_1_out));
  Transistor #(.\type ("n")) transistor_4 (.in(transistor_6_out), .out(transistor_1_out), .gate(input0));
  Transistor #(.\type ("n")) transistor_5 (.in(1'b0), .out(transistor_3_out), .gate(transistor_1_out));
  Transistor #(.\type ("n")) transistor_6 (.in(1'b0), .out(transistor_6_out), .gate(input1));
  Transistor transistor_7 (.in(1'b1), .out(transistor_7_out), .gate(input2));
  Transistor transistor_8 (.in(1'b1), .out(transistor_7_out), .gate(transistor_3_out));
  Transistor #(.\type ("n")) transistor_9 (.in(transistor_10_out), .out(transistor_7_out), .gate(transistor_3_out));
  Transistor #(.\type ("n")) transistor_10 (.in(1'b0), .out(transistor_10_out), .gate(input2));
  Transistor transistor_11 (.in(1'b1), .out(output0), .gate(transistor_7_out));
  Transistor #(.\type ("n")) transistor_12 (.in(1'b0), .out(output0), .gate(transistor_7_out));
endmodule
