// Logisim project AND gate.circ as structural Verilog: 1 circuit, main circuit main
module main (
  input  inputA,
  input  inputB,
  output outputY
);

  wire transistor_1_out, transistor_6_out;

  Transistor transistor_1 (.in(1'b1), .out(transistor_1_out), .gate(inputB));
  Transistor transistor_2 (.in(1'b1), .out(transistor_1_out), .gate(inputA));
  Transistor transistor_3 (.in(1'b1), .out(outputY), .gate(transistor_1_out));
  Transistor #(.\type ("n")) transistor_4 (.in(transistor_6_out), .out(transistor_1_out), .gate(inputA));
  Transistor #(.\type ("n")) transistor_5 (.in(1'b0), .out(outputY), .gate(transistor_1_out));
  Transistor #(.\type ("n")) transistor_6 (.in(1'b0), .out(transistor_6_out), .gate(inputB));
endmodule
