// Logisim project NAND gate.circ as structural Verilog: 1 circuit, main circuit main
module main (
  input  inputA,
  input  inputB,
  output outputY
);

  wire transistor_4_out;

  Transistor transistor_1 (.in(1'b1), .out(outputY), .gate(inputB));
  Transistor transistor_2 (.in(1'b1), .out(outputY), .gate(inputA));
  Transistor #(.\type ("n")) transistor_3 (.in(transistor_4_out), .out(outputY), .gate(inputA));
  Transistor #(.\type ("n")) transistor_4 (.in(1'b0), .out(transistor_4_out), .gate(inputB));
endmodule
