// Logisim project NIMPLY gate.circ as structural Verilog: 1 circuit, main circuit main
module main (
  input  input0,
  input  input1,
  output output0
);

  wire transistor_1_out, transistor_3_out, transistor_6_out;

  Transistor transistor_1 (.in(1'b1), .out(transistor_1_out), .gate(input1));
  Transistor #(.\type ("n")) transistor_2 (.in(1'b0), .out(transistor_1_out), .gate(input1));
  Transistor transistor_3 (.in(1'b1), .out(transistor_3_out), .gate(transistor_1_out));
  Transistor transistor_4 (.in(1'b1), .out(transistor_3_out), .gate(input0));
  Transistor #(.\type ("n")) transistor_5 (.in(transistor_6_out), .out(transistor_3_out), .gate(input0));
  Transistor #(.\type ("n")) transistor_6 (.in(1'b0), .out(transistor_6_out), .gate(transistor_1_out));
  Transistor transistor_7 (.in(1'b1), .out(output0), .gate(transistor_3_out));
  Transistor #(.\type ("n")) transistor_8 (.in(1'b0), .out(output0), .gate(transistor_3_out));
endmodule
