// Logisim project NOR gate.circ as structural Verilog: 1 circuit, main circuit main
module main (
  input  inputA,
  input  inputB,
  output outputY
);

  wire transistor_2_out;

  Transistor #(.\type ("n")) transistor_1 (.in(1'b0), .out(outputY), .gate(inputA));
  Transistor transistor_2 (.in(1'b1), .out(transistor_2_out), .gate(inputA));
  Transistor transistor_3 (.in(transistor_2_out), .out(outputY), .gate(inputB));
  Transistor #(.\type ("n")) transistor_4 (.in(1'b0), .out(outputY), .gate(inputB));
endmodule
