// Logisim project OR gate 3-bit input slow.circ as structural Verilog: 1 circuit, main circuit main
module main (
  input  input0,
  input  input1,
  input  input2,
  output output0
);

  wire transistor_1_out, transistor_2_out, transistor_4_out, transistor_7_out, transistor_8_out;

  Transistor #(.\type ("n")) transistor_1 (.in(1'b0), .out(transistor_1_out), .gate(input1));
  Transistor transistor_2 (.in(1'b1), .out(transistor_2_out), .gate(input1));
  Transistor transistor_3 (.in(transistor_2_out), .out(transistor_1_out), .gate(input2));
  Transistor transistor_4 (.in(1'b1), .out(transistor_4_out), .gate(transistor_1_out));
  Transistor #(.\type ("n")) transistor_5 (.in(1'b0), .out(transistor_1_out), .gate(input2));
  Transistor #(.\type ("n")) transistor_6 (.in(1'b0), .out(transistor_4_out), .gate(transistor_1_out));
  Transistor #(.\type ("n")) transistor_7 (.in(1'b0), .out(transistor_7_out), .gate(input0));
  Transistor transistor_8 (.in(1'b1), .out(transistor_8_out), .gate(input0));
  Transistor transistor_9 (.in(transistor_8_out), .out(transistor_7_out), .gate(transistor_4_out));
  Transistor #(.\type ("n")) transistor_10 (.in(1'b0), .out(transistor_7_out), .gate(transistor_4_out));
  Transistor transistor_11 (.in(1'b1), .out(output0), .gate(transistor_7_out));
  Transistor #(.\type ("n")) transistor_12 (.in(1'b0), .out(output0), .gate(transistor_7_out));
endmodule
