// Logisim project OR gate.circ as structural Verilog: 1 circuit, main circuit main
module main (
  input  inputA,
  input  inputB,
  output outputY
);

  wire transistor_1_out, transistor_2_out;

  Transistor #(.\type ("n")) transistor_1 (.in(1'b0), .out(transistor_1_out), .gate(inputA));
  Transistor transistor_2 (.in(1'b1), .out(transistor_2_out), .gate(inputA));
  Transistor transistor_3 (.in(transistor_2_out), .out(transistor_1_out), .gate(inputB));
  Transistor #(.\type ("n")) transistor_4 (.in(1'b0), .out(transistor_1_out), .gate(inputB));
  Transistor transistor_5 (.in(1'b1), .out(outputY), .gate(transistor_1_out));
  Transistor #(.\type ("n")) transistor_6 (.in(1'b0), .out(outputY), .gate(transistor_1_out));
endmodule
