// Logisim project Transmission gate.circ as structural Verilog: 1 circuit, main circuit main
module main (
  input  input_Control0_S,
  input  input0_S,
  input  input_Control0_D,
  input  input0_D,
  output output0_S,
  output output0_D
);

  wire transistor_1_out, transistor_3_out;

  Transistor transistor_1 (.in(1'b1), .out(transistor_1_out), .gate(input_Control0_S));
  Transistor #(.\type ("n")) transistor_2 (.in(1'b0), .out(transistor_1_out), .gate(input_Control0_S));
  Transistor transistor_3 (.in(1'b1), .out(transistor_3_out), .gate(input_Control0_D));
  Transistor #(.\type ("n")) transistor_4 (.in(1'b0), .out(transistor_3_out), .gate(input_Control0_D));
  Transistor transistor_5 (.in(input0_S), .out(output0_S), .gate(transistor_1_out));
  Transistor #(.\type ("n")) transistor_6 (.in(input0_S), .out(output0_S), .gate(input_Control0_S));
  Transistor transistor_7 (.in(input0_D), .out(output0_D), .gate(transistor_3_out));
  Transistor #(.\type ("n")) transistor_8 (.in(input0_D), .out(output0_D), .gate(input_Control0_D));

  // Notes on the sheet:
  //   Sources as output
  //   Drains as output
  //   P
endmodule
