// Logisim project Tri-state gate.circ as structural Verilog: 1 circuit, main circuit main
module main (
  input  input0_nand,
  input  input0_not,
  input  control_nand,
  input  control_not,
  input  input0_C1,
  input  input0_tg,
  input  control_C1,
  input  control_tg,
  input  input0_nor,
  input  control_nor,
  output output0_nand,
  output output0_not,
  output output0_C1,
  output output0_tg,
  output output0_nor
);

  wire transistor_1_out, transistor_2_out, transistor_5_out, transistor_6_out, transistor_11_out,
       transistor_12_out, transistor_15_out, transistor_17_out, transistor_21_out, transistor_24_out,
       transistor_25_out;

  Transistor transistor_1 (.in(1'b1), .out(transistor_1_out), .gate(control_nand));
  Transistor #(.\type ("n")) transistor_2 (.in(1'b0), .out(transistor_2_out), .gate(control_nor));
  Transistor transistor_3 (.in(1'b1), .out(transistor_1_out), .gate(input0_nand));
  Transistor #(.\type ("n")) transistor_4 (.in(transistor_5_out), .out(transistor_1_out), .gate(input0_nand));
  Transistor #(.\type ("n")) transistor_5 (.in(1'b0), .out(transistor_5_out), .gate(control_nand));
  Transistor transistor_6 (.in(1'b1), .out(transistor_6_out), .gate(control_nor));
  Transistor transistor_7 (.in(transistor_6_out), .out(transistor_2_out), .gate(input0_nor));
  Transistor #(.\type ("n")) transistor_8 (.in(1'b0), .out(transistor_2_out), .gate(input0_nor));
  Transistor transistor_9 (.in(1'b1), .out(output0_nand), .gate(transistor_1_out));
  Transistor #(.\type ("n")) transistor_10 (.in(transistor_11_out), .out(output0_nand), .gate(transistor_1_out));
  Transistor #(.\type ("n")) transistor_11 (.in(1'b0), .out(transistor_11_out), .gate(control_nand));
  Transistor transistor_12 (.in(1'b1), .out(transistor_12_out), .gate(control_nor));
  Transistor transistor_13 (.in(transistor_12_out), .out(output0_nor), .gate(transistor_2_out));
  Transistor #(.\type ("n")) transistor_14 (.in(1'b0), .out(output0_nor), .gate(transistor_2_out));
  Transistor transistor_15 (.in(1'b1), .out(transistor_15_out), .gate(control_tg));
  Transistor #(.\type ("n")) transistor_16 (.in(1'b0), .out(transistor_15_out), .gate(control_tg));
  Transistor transistor_17 (.in(1'b1), .out(transistor_17_out), .gate(control_not));
  Transistor #(.\type ("n")) transistor_18 (.in(1'b0), .out(transistor_17_out), .gate(control_not));
  Transistor transistor_19 (.in(input0_tg), .out(output0_tg), .gate(transistor_15_out));
  Transistor #(.\type ("n")) transistor_20 (.in(input0_tg), .out(output0_tg), .gate(control_tg));
  Transistor transistor_21 (.in(1'b1), .out(transistor_21_out), .gate(transistor_17_out));
  Transistor transistor_22 (.in(transistor_21_out), .out(output0_not), .gate(input0_not));
  Transistor #(.\type ("n")) transistor_23 (.in(transistor_24_out), .out(output0_not), .gate(input0_not));
  Transistor #(.\type ("n")) transistor_24 (.in(1'b0), .out(transistor_24_out), .gate(control_not));
  Transistor transistor_25 (.in(1'b1), .out(transistor_25_out), .gate(control_C1));
  Transistor #(.\type ("n")) transistor_26 (.in(1'b0), .out(transistor_25_out), .gate(control_C1));
  Transistor transistor_27 (.in(input0_C1), .out(output0_C1), .gate(transistor_25_out));
  Transistor #(.\type ("n")) transistor_28 (.in(input0_C1), .out(output0_C1), .gate(control_C1));

  // Notes on the sheet:
  //   Control with NAND gate
  //   Control with NOR gate
  //   Control with NOT gate
  //   Control with Transmission gate
endmodule
