// Logisim project XNOR gate.circ as structural Verilog: 1 circuit, main circuit main
module main (
  input  input0_A,
  input  input0_B,
  input  input1_A,
  input  input1_B,
  input  input0_C,
  input  input1_C,
  output output0_A,
  output output0_B,
  output output0_C
);

  wire transistor_1_out, transistor_5_out, transistor_9_out, transistor_11_out, transistor_17_out,
       transistor_19_out;

  Transistor transistor_1 (.in(input0_A), .out(transistor_1_out), .gate(input1_A));
  Transistor transistor_2 (.in(input1_A), .out(transistor_1_out), .gate(input0_A));
  Transistor #(.\type ("n")) transistor_3 (.in(transistor_9_out), .out(transistor_1_out), .gate(input1_A));
  Transistor #(.\type ("n")) transistor_4 (.in(input1_A), .out(transistor_1_out), .gate(transistor_9_out));
  Transistor transistor_5 (.in(input0_C), .out(transistor_5_out), .gate(input1_C));
  Transistor #(.\type ("n")) transistor_6 (.in(transistor_11_out), .out(transistor_5_out), .gate(input1_C));
  Transistor transistor_7 (.in(input1_C), .out(transistor_5_out), .gate(input0_C));
  Transistor #(.\type ("n")) transistor_8 (.in(input1_C), .out(transistor_5_out), .gate(transistor_11_out));
  Transistor transistor_9 (.in(1'b1), .out(transistor_9_out), .gate(input0_A));
  Transistor #(.\type ("n")) transistor_10 (.in(1'b0), .out(transistor_9_out), .gate(input0_A));
  Transistor transistor_11 (.in(1'b1), .out(transistor_11_out), .gate(input0_C));
  Transistor #(.\type ("n")) transistor_12 (.in(1'b0), .out(transistor_11_out), .gate(input0_C));
  Transistor transistor_13 (.in(1'b1), .out(output0_A), .gate(transistor_1_out));
  Transistor #(.\type ("n")) transistor_14 (.in(1'b0), .out(output0_A), .gate(transistor_1_out));
  Transistor transistor_15 (.in(1'b1), .out(output0_C), .gate(transistor_5_out));
  Transistor #(.\type ("n")) transistor_16 (.in(1'b0), .out(output0_C), .gate(transistor_5_out));
  Transistor transistor_17 (.in(1'b1), .out(transistor_17_out), .gate(input0_B));
  Transistor #(.\type ("n")) transistor_18 (.in(1'b0), .out(transistor_17_out), .gate(input0_B));
  Transistor transistor_19 (.in(input0_B), .out(transistor_19_out), .gate(input1_B));
  Transistor #(.\type ("n")) transistor_20 (.in(transistor_17_out), .out(transistor_19_out), .gate(input1_B));
  Transistor transistor_21 (.in(input1_B), .out(transistor_19_out), .gate(input0_B));
  Transistor #(.\type ("n")) transistor_22 (.in(input1_B), .out(transistor_19_out), .gate(transistor_17_out));
  Transistor transistor_23 (.in(1'b1), .out(output0_B), .gate(transistor_19_out));
  Transistor #(.\type ("n")) transistor_24 (.in(1'b0), .out(output0_B), .gate(transistor_19_out));
endmodule
