// Logisim project XOR gate.circ as structural Verilog: 1 circuit, main circuit main
module main (
  input  input0_B,
  input  input0_A,
  input  input1_A,
  input  input1_B,
  input  input0_C,
  input  input1_C,
  output output0_A,
  output output0_B,
  output output0_C
);

  wire transistor_9_out, transistor_11_out, transistor_13_out;

  Transistor transistor_1 (.in(input0_A), .out(output0_A), .gate(input1_A));
  Transistor transistor_2 (.in(input1_A), .out(output0_A), .gate(input0_A));
  Transistor #(.\type ("n")) transistor_3 (.in(transistor_9_out), .out(output0_A), .gate(input1_A));
  Transistor #(.\type ("n")) transistor_4 (.in(input1_A), .out(output0_A), .gate(transistor_9_out));
  Transistor transistor_5 (.in(input0_C), .out(output0_C), .gate(input1_C));
  Transistor #(.\type ("n")) transistor_6 (.in(transistor_11_out), .out(output0_C), .gate(input1_C));
  Transistor transistor_7 (.in(input1_C), .out(output0_C), .gate(input0_C));
  Transistor #(.\type ("n")) transistor_8 (.in(input1_C), .out(output0_C), .gate(transistor_11_out));
  Transistor transistor_9 (.in(1'b1), .out(transistor_9_out), .gate(input0_A));
  Transistor #(.\type ("n")) transistor_10 (.in(1'b0), .out(transistor_9_out), .gate(input0_A));
  Transistor transistor_11 (.in(1'b1), .out(transistor_11_out), .gate(input0_C));
  Transistor #(.\type ("n")) transistor_12 (.in(1'b0), .out(transistor_11_out), .gate(input0_C));
  Transistor transistor_13 (.in(1'b1), .out(transistor_13_out), .gate(input0_B));
  Transistor #(.\type ("n")) transistor_14 (.in(1'b0), .out(transistor_13_out), .gate(input0_B));
  Transistor transistor_15 (.in(input0_B), .out(output0_B), .gate(input1_B));
  Transistor #(.\type ("n")) transistor_16 (.in(transistor_13_out), .out(output0_B), .gate(input1_B));
  Transistor transistor_17 (.in(input1_B), .out(output0_B), .gate(input0_B));
  Transistor #(.\type ("n")) transistor_18 (.in(input1_B), .out(output0_B), .gate(transistor_13_out));
endmodule
