// Logisim project AND gate all cases.circ as structural Verilog: 1 circuit, main circuit main
module main (
  output output0_C0,
  output output0_C2,
  output output0_C1,
  output output0_C3
);

  wire transistor_1_out, transistor_2_out, transistor_7_out, transistor_12_out, transistor_13_out,
       transistor_16_out, transistor_17_out, transistor_20_out;

  Transistor transistor_1 (.in(1'b1), .out(transistor_1_out), .gate(1'b0));
  Transistor transistor_2 (.in(1'b1), .out(transistor_2_out), .gate(1'b1));
  Transistor transistor_3 (.in(1'b1), .out(transistor_1_out), .gate(1'b0));
  Transistor transistor_4 (.in(1'b1), .out(output0_C0), .gate(transistor_1_out));
  Transistor #(.\type ("n")) transistor_5 (.in(transistor_7_out), .out(transistor_1_out), .gate(1'b0));
  Transistor #(.\type ("n")) transistor_6 (.in(1'b0), .out(output0_C0), .gate(transistor_1_out));
  Transistor #(.\type ("n")) transistor_7 (.in(1'b0), .out(transistor_7_out), .gate(1'b0));
  Transistor transistor_8 (.in(1'b1), .out(transistor_2_out), .gate(1'b0));
  Transistor transistor_9 (.in(1'b1), .out(output0_C1), .gate(transistor_2_out));
  Transistor #(.\type ("n")) transistor_10 (.in(transistor_12_out), .out(transistor_2_out), .gate(1'b0));
  Transistor #(.\type ("n")) transistor_11 (.in(1'b0), .out(output0_C1), .gate(transistor_2_out));
  Transistor #(.\type ("n")) transistor_12 (.in(1'b0), .out(transistor_12_out), .gate(1'b1));
  Transistor transistor_13 (.in(1'b1), .out(transistor_13_out), .gate(1'b0));
  Transistor transistor_14 (.in(1'b1), .out(transistor_13_out), .gate(1'b1));
  Transistor #(.\type ("n")) transistor_15 (.in(transistor_16_out), .out(transistor_13_out), .gate(1'b1));
  Transistor #(.\type ("n")) transistor_16 (.in(1'b0), .out(transistor_16_out), .gate(1'b0));
  Transistor transistor_17 (.in(1'b1), .out(transistor_17_out), .gate(1'b1));
  Transistor transistor_18 (.in(1'b1), .out(transistor_17_out), .gate(1'b1));
  Transistor #(.\type ("n")) transistor_19 (.in(transistor_20_out), .out(transistor_17_out), .gate(1'b1));
  Transistor #(.\type ("n")) transistor_20 (.in(1'b0), .out(transistor_20_out), .gate(1'b1));
  Transistor transistor_21 (.in(1'b1), .out(output0_C2), .gate(transistor_13_out));
  Transistor #(.\type ("n")) transistor_22 (.in(1'b0), .out(output0_C2), .gate(transistor_13_out));
  Transistor transistor_23 (.in(1'b1), .out(output0_C3), .gate(transistor_17_out));
  Transistor #(.\type ("n")) transistor_24 (.in(1'b0), .out(output0_C3), .gate(transistor_17_out));

  // Notes on the sheet:
  //   input0
  //   input1
  //   input0
  //   input1
  //   input0
  //   input1
  //   input0
  //   input1
endmodule
