// Logisim project NAND gate all cases.circ as structural Verilog: 1 circuit, main circuit main
module main (
  output output0_C0,
  output output0_C2,
  output output0_C1,
  output output0_C3
);

  wire transistor_5_out, transistor_8_out, transistor_12_out, transistor_16_out;

  Transistor transistor_1 (.in(1'b1), .out(output0_C0), .gate(1'b0));
  Transistor transistor_2 (.in(1'b1), .out(output0_C1), .gate(1'b1));
  Transistor transistor_3 (.in(1'b1), .out(output0_C0), .gate(1'b0));
  Transistor #(.\type ("n")) transistor_4 (.in(transistor_5_out), .out(output0_C0), .gate(1'b0));
  Transistor #(.\type ("n")) transistor_5 (.in(1'b0), .out(transistor_5_out), .gate(1'b0));
  Transistor transistor_6 (.in(1'b1), .out(output0_C1), .gate(1'b0));
  Transistor #(.\type ("n")) transistor_7 (.in(transistor_8_out), .out(output0_C1), .gate(1'b0));
  Transistor #(.\type ("n")) transistor_8 (.in(1'b0), .out(transistor_8_out), .gate(1'b1));
  Transistor transistor_9 (.in(1'b1), .out(output0_C2), .gate(1'b0));
  Transistor transistor_10 (.in(1'b1), .out(output0_C2), .gate(1'b1));
  Transistor #(.\type ("n")) transistor_11 (.in(transistor_12_out), .out(output0_C2), .gate(1'b1));
  Transistor #(.\type ("n")) transistor_12 (.in(1'b0), .out(transistor_12_out), .gate(1'b0));
  Transistor transistor_13 (.in(1'b1), .out(output0_C3), .gate(1'b1));
  Transistor transistor_14 (.in(1'b1), .out(output0_C3), .gate(1'b1));
  Transistor #(.\type ("n")) transistor_15 (.in(transistor_16_out), .out(output0_C3), .gate(1'b1));
  Transistor #(.\type ("n")) transistor_16 (.in(1'b0), .out(transistor_16_out), .gate(1'b1));

  // Notes on the sheet:
  //   input0
  //   input1
  //   input0
  //   input1
  //   input0
  //   input1
  //   input0
  //   input1
endmodule
