// Logisim project NOR gate all cases.circ as structural Verilog: 1 circuit, main circuit main
module main (
  output output0_C0,
  output output0_C2,
  output output0_C1,
  output output0_C3
);

  wire transistor_2_out, transistor_6_out, transistor_10_out, transistor_14_out;

  Transistor #(.\type ("n")) transistor_1 (.in(1'b0), .out(output0_C1), .gate(1'b0));
  Transistor transistor_2 (.in(1'b1), .out(transistor_2_out), .gate(1'b0));
  Transistor transistor_3 (.in(transistor_2_out), .out(output0_C0), .gate(1'b0));
  Transistor #(.\type ("n")) transistor_4 (.in(1'b0), .out(output0_C0), .gate(1'b0));
  Transistor #(.\type ("n")) transistor_5 (.in(1'b0), .out(output0_C0), .gate(1'b0));
  Transistor transistor_6 (.in(1'b1), .out(transistor_6_out), .gate(1'b0));
  Transistor transistor_7 (.in(transistor_6_out), .out(output0_C1), .gate(1'b1));
  Transistor #(.\type ("n")) transistor_8 (.in(1'b0), .out(output0_C1), .gate(1'b1));
  Transistor #(.\type ("n")) transistor_9 (.in(1'b0), .out(output0_C3), .gate(1'b1));
  Transistor transistor_10 (.in(1'b1), .out(transistor_10_out), .gate(1'b1));
  Transistor transistor_11 (.in(transistor_10_out), .out(output0_C2), .gate(1'b0));
  Transistor #(.\type ("n")) transistor_12 (.in(1'b0), .out(output0_C2), .gate(1'b1));
  Transistor #(.\type ("n")) transistor_13 (.in(1'b0), .out(output0_C2), .gate(1'b0));
  Transistor transistor_14 (.in(1'b1), .out(transistor_14_out), .gate(1'b1));
  Transistor transistor_15 (.in(transistor_14_out), .out(output0_C3), .gate(1'b1));
  Transistor #(.\type ("n")) transistor_16 (.in(1'b0), .out(output0_C3), .gate(1'b1));

  // Notes on the sheet:
  //   input0
  //   input1
  //   input0
  //   input1
  //   input0
  //   input1
  //   input0
  //   input1
endmodule
