// Logisim project NOT gate all cases.circ as structural Verilog: 1 circuit, main circuit main
module main (
  output output0_C0,
  output output0_C1
);

  Transistor transistor_1 (.in(1'b1), .out(output0_C0), .gate(1'b1));
  Transistor #(.\type ("n")) transistor_2 (.in(1'b0), .out(output0_C0), .gate(1'b1));
  Transistor transistor_3 (.in(1'b1), .out(output0_C1), .gate(1'b0));
  Transistor #(.\type ("n")) transistor_4 (.in(1'b0), .out(output0_C1), .gate(1'b0));

  // Notes on the sheet:
  //   input
  //   input
endmodule
