// Logisim project OR gate all cases.circ as structural Verilog: 1 circuit, main circuit main
module main (
  output output0_C0,
  output output0_C2,
  output output0_C1,
  output output0_C3
);

  wire transistor_1_out, transistor_2_out, transistor_3_out, transistor_8_out, transistor_13_out,
       transistor_14_out, transistor_17_out, transistor_18_out;

  Transistor #(.\type ("n")) transistor_1 (.in(1'b0), .out(transistor_1_out), .gate(1'b0));
  Transistor #(.\type ("n")) transistor_2 (.in(1'b0), .out(transistor_2_out), .gate(1'b1));
  Transistor transistor_3 (.in(1'b1), .out(transistor_3_out), .gate(1'b0));
  Transistor transistor_4 (.in(transistor_3_out), .out(transistor_1_out), .gate(1'b0));
  Transistor transistor_5 (.in(1'b1), .out(output0_C0), .gate(transistor_1_out));
  Transistor #(.\type ("n")) transistor_6 (.in(1'b0), .out(transistor_1_out), .gate(1'b0));
  Transistor #(.\type ("n")) transistor_7 (.in(1'b0), .out(output0_C0), .gate(transistor_1_out));
  Transistor transistor_8 (.in(1'b1), .out(transistor_8_out), .gate(1'b1));
  Transistor transistor_9 (.in(transistor_8_out), .out(transistor_2_out), .gate(1'b0));
  Transistor transistor_10 (.in(1'b1), .out(output0_C1), .gate(transistor_2_out));
  Transistor #(.\type ("n")) transistor_11 (.in(1'b0), .out(transistor_2_out), .gate(1'b0));
  Transistor #(.\type ("n")) transistor_12 (.in(1'b0), .out(output0_C1), .gate(transistor_2_out));
  Transistor transistor_13 (.in(1'b1), .out(transistor_13_out), .gate(1'b0));
  Transistor transistor_14 (.in(transistor_13_out), .out(transistor_14_out), .gate(1'b1));
  Transistor #(.\type ("n")) transistor_15 (.in(1'b0), .out(transistor_14_out), .gate(1'b0));
  Transistor #(.\type ("n")) transistor_16 (.in(1'b0), .out(transistor_14_out), .gate(1'b1));
  Transistor transistor_17 (.in(1'b1), .out(transistor_17_out), .gate(1'b1));
  Transistor transistor_18 (.in(transistor_17_out), .out(transistor_18_out), .gate(1'b1));
  Transistor #(.\type ("n")) transistor_19 (.in(1'b0), .out(transistor_18_out), .gate(1'b1));
  Transistor #(.\type ("n")) transistor_20 (.in(1'b0), .out(transistor_18_out), .gate(1'b1));
  Transistor transistor_21 (.in(1'b1), .out(output0_C2), .gate(transistor_14_out));
  Transistor #(.\type ("n")) transistor_22 (.in(1'b0), .out(output0_C2), .gate(transistor_14_out));
  Transistor transistor_23 (.in(1'b1), .out(output0_C3), .gate(transistor_18_out));
  Transistor #(.\type ("n")) transistor_24 (.in(1'b0), .out(output0_C3), .gate(transistor_18_out));

  // Notes on the sheet:
  //   input0
  //   input1
  //   input0
  //   input1
  //   input0
  //   input1
  //   input0
  //   input1
endmodule
