// Logisim project Transmission gate all cases.circ as structural Verilog: 1 circuit, main circuit main
module main (
  output output0_C0,
  output output0_C2,
  output output0_C1,
  output output0_C3
);

  wire transistor_1_out, transistor_3_out, transistor_9_out, transistor_11_out;

  Transistor transistor_1 (.in(1'b1), .out(transistor_1_out), .gate(1'b0));
  Transistor #(.\type ("n")) transistor_2 (.in(1'b0), .out(transistor_1_out), .gate(1'b0));
  Transistor transistor_3 (.in(1'b1), .out(transistor_3_out), .gate(1'b0));
  Transistor #(.\type ("n")) transistor_4 (.in(1'b0), .out(transistor_3_out), .gate(1'b0));
  Transistor transistor_5 (.in(1'b0), .out(output0_C0), .gate(transistor_1_out));
  Transistor #(.\type ("n")) transistor_6 (.in(1'b0), .out(output0_C0), .gate(1'b0));
  Transistor transistor_7 (.in(1'b1), .out(output0_C1), .gate(transistor_3_out));
  Transistor #(.\type ("n")) transistor_8 (.in(1'b1), .out(output0_C1), .gate(1'b0));
  Transistor transistor_9 (.in(1'b1), .out(transistor_9_out), .gate(1'b1));
  Transistor #(.\type ("n")) transistor_10 (.in(1'b0), .out(transistor_9_out), .gate(1'b1));
  Transistor transistor_11 (.in(1'b1), .out(transistor_11_out), .gate(1'b1));
  Transistor #(.\type ("n")) transistor_12 (.in(1'b0), .out(transistor_11_out), .gate(1'b1));
  Transistor transistor_13 (.in(1'b0), .out(output0_C2), .gate(transistor_9_out));
  Transistor #(.\type ("n")) transistor_14 (.in(1'b0), .out(output0_C2), .gate(1'b1));
  Transistor transistor_15 (.in(1'b1), .out(output0_C3), .gate(transistor_11_out));
  Transistor #(.\type ("n")) transistor_16 (.in(1'b1), .out(output0_C3), .gate(1'b1));

  // Notes on the sheet:
  //   control
  //   input0
  //   control
  //   input0
  //   control
  //   input0
  //   control
  //   input0
endmodule
