// Logisim project Tri-state gate all cases.circ as structural Verilog: 1 circuit, main circuit main
module main (
  output output0_nand_C0,
  output output0_nand_C2,
  output output0_nand_C1,
  output output0_nand_C3,
  output output0_nor_C0,
  output output0_nor_C2,
  output output0_nor_C1,
  output output0_nor_C3,
  output output0_not_C0,
  output output0_not_C2,
  output output0_not_C1,
  output output0_not_C3,
  output output0_tg_C0,
  output output0_tg_C2,
  output output0_tg_C1,
  output output0_tg_C3
);

  wire transistor_1_out, transistor_2_out, transistor_3_out, transistor_4_out, transistor_5_out,
       transistor_7_out, transistor_11_out, transistor_14_out, transistor_15_out, transistor_18_out,
       transistor_21_out, transistor_22_out, transistor_26_out, transistor_27_out, transistor_28_out,
       transistor_32_out, transistor_35_out, transistor_38_out, transistor_39_out, transistor_42_out,
       transistor_49_out, transistor_50_out, transistor_51_out, transistor_53_out, transistor_55_out,
       transistor_58_out, transistor_59_out, transistor_62_out, transistor_63_out, transistor_66_out,
       transistor_69_out, transistor_71_out, transistor_75_out, transistor_78_out, transistor_79_out,
       transistor_82_out, transistor_85_out, transistor_88_out, transistor_89_out, transistor_92_out;

  Transistor transistor_1 (.in(1'b1), .out(transistor_1_out), .gate(1'b0));
  Transistor transistor_2 (.in(1'b1), .out(transistor_2_out), .gate(1'b1));
  Transistor #(.\type ("n")) transistor_3 (.in(1'b0), .out(transistor_3_out), .gate(1'b0));
  Transistor #(.\type ("n")) transistor_4 (.in(1'b0), .out(transistor_4_out), .gate(1'b1));
  Transistor transistor_5 (.in(1'b1), .out(transistor_5_out), .gate(1'b0));
  Transistor #(.\type ("n")) transistor_6 (.in(1'b0), .out(transistor_5_out), .gate(1'b0));
  Transistor transistor_7 (.in(1'b1), .out(transistor_7_out), .gate(1'b1));
  Transistor #(.\type ("n")) transistor_8 (.in(1'b0), .out(transistor_7_out), .gate(1'b1));
  Transistor transistor_9 (.in(1'b1), .out(transistor_1_out), .gate(1'b0));
  Transistor #(.\type ("n")) transistor_10 (.in(transistor_11_out), .out(transistor_1_out), .gate(1'b0));
  Transistor #(.\type ("n")) transistor_11 (.in(1'b0), .out(transistor_11_out), .gate(1'b0));
  Transistor transistor_12 (.in(1'b1), .out(transistor_2_out), .gate(1'b0));
  Transistor #(.\type ("n")) transistor_13 (.in(transistor_14_out), .out(transistor_2_out), .gate(1'b0));
  Transistor #(.\type ("n")) transistor_14 (.in(1'b0), .out(transistor_14_out), .gate(1'b1));
  Transistor transistor_15 (.in(1'b1), .out(transistor_15_out), .gate(1'b0));
  Transistor transistor_16 (.in(transistor_15_out), .out(transistor_3_out), .gate(1'b0));
  Transistor #(.\type ("n")) transistor_17 (.in(1'b0), .out(transistor_3_out), .gate(1'b0));
  Transistor transistor_18 (.in(1'b1), .out(transistor_18_out), .gate(1'b1));
  Transistor transistor_19 (.in(transistor_18_out), .out(transistor_4_out), .gate(1'b0));
  Transistor #(.\type ("n")) transistor_20 (.in(1'b0), .out(transistor_4_out), .gate(1'b0));
  Transistor transistor_21 (.in(1'b1), .out(transistor_21_out), .gate(1'b0));
  Transistor transistor_22 (.in(1'b1), .out(transistor_22_out), .gate(transistor_21_out));
  Transistor #(.\type ("n")) transistor_23 (.in(1'b0), .out(transistor_21_out), .gate(1'b0));
  Transistor transistor_24 (.in(transistor_22_out), .out(output0_not_C0), .gate(1'b0));
  Transistor #(.\type ("n")) transistor_25 (.in(transistor_26_out), .out(output0_not_C0), .gate(1'b0));
  Transistor #(.\type ("n")) transistor_26 (.in(1'b0), .out(transistor_26_out), .gate(1'b0));
  Transistor transistor_27 (.in(1'b1), .out(transistor_27_out), .gate(1'b1));
  Transistor transistor_28 (.in(1'b1), .out(transistor_28_out), .gate(transistor_27_out));
  Transistor #(.\type ("n")) transistor_29 (.in(1'b0), .out(transistor_27_out), .gate(1'b1));
  Transistor transistor_30 (.in(transistor_28_out), .out(output0_not_C1), .gate(1'b0));
  Transistor #(.\type ("n")) transistor_31 (.in(transistor_32_out), .out(output0_not_C1), .gate(1'b0));
  Transistor #(.\type ("n")) transistor_32 (.in(1'b0), .out(transistor_32_out), .gate(1'b1));
  Transistor transistor_33 (.in(1'b1), .out(output0_nand_C0), .gate(transistor_1_out));
  Transistor #(.\type ("n")) transistor_34 (.in(transistor_35_out), .out(output0_nand_C0), .gate(transistor_1_out));
  Transistor #(.\type ("n")) transistor_35 (.in(1'b0), .out(transistor_35_out), .gate(1'b0));
  Transistor transistor_36 (.in(1'b1), .out(output0_nand_C1), .gate(transistor_2_out));
  Transistor #(.\type ("n")) transistor_37 (.in(transistor_38_out), .out(output0_nand_C1), .gate(transistor_2_out));
  Transistor #(.\type ("n")) transistor_38 (.in(1'b0), .out(transistor_38_out), .gate(1'b1));
  Transistor transistor_39 (.in(1'b1), .out(transistor_39_out), .gate(1'b0));
  Transistor transistor_40 (.in(transistor_39_out), .out(output0_nor_C0), .gate(transistor_3_out));
  Transistor #(.\type ("n")) transistor_41 (.in(1'b0), .out(output0_nor_C0), .gate(transistor_3_out));
  Transistor transistor_42 (.in(1'b1), .out(transistor_42_out), .gate(1'b1));
  Transistor transistor_43 (.in(transistor_42_out), .out(output0_nor_C1), .gate(transistor_4_out));
  Transistor #(.\type ("n")) transistor_44 (.in(1'b0), .out(output0_nor_C1), .gate(transistor_4_out));
  Transistor transistor_45 (.in(1'b0), .out(output0_tg_C0), .gate(transistor_5_out));
  Transistor #(.\type ("n")) transistor_46 (.in(1'b0), .out(output0_tg_C0), .gate(1'b0));
  Transistor transistor_47 (.in(1'b0), .out(output0_tg_C1), .gate(transistor_7_out));
  Transistor #(.\type ("n")) transistor_48 (.in(1'b0), .out(output0_tg_C1), .gate(1'b1));
  Transistor #(.\type ("n")) transistor_49 (.in(1'b0), .out(transistor_49_out), .gate(1'b0));
  Transistor #(.\type ("n")) transistor_50 (.in(1'b0), .out(transistor_50_out), .gate(1'b1));
  Transistor transistor_51 (.in(1'b1), .out(transistor_51_out), .gate(1'b0));
  Transistor #(.\type ("n")) transistor_52 (.in(1'b0), .out(transistor_51_out), .gate(1'b0));
  Transistor transistor_53 (.in(1'b1), .out(transistor_53_out), .gate(1'b1));
  Transistor #(.\type ("n")) transistor_54 (.in(1'b0), .out(transistor_53_out), .gate(1'b1));
  Transistor transistor_55 (.in(1'b1), .out(transistor_55_out), .gate(1'b0));
  Transistor transistor_56 (.in(1'b1), .out(transistor_55_out), .gate(1'b1));
  Transistor #(.\type ("n")) transistor_57 (.in(transistor_58_out), .out(transistor_55_out), .gate(1'b1));
  Transistor #(.\type ("n")) transistor_58 (.in(1'b0), .out(transistor_58_out), .gate(1'b0));
  Transistor transistor_59 (.in(1'b1), .out(transistor_59_out), .gate(1'b1));
  Transistor transistor_60 (.in(1'b1), .out(transistor_59_out), .gate(1'b1));
  Transistor #(.\type ("n")) transistor_61 (.in(transistor_62_out), .out(transistor_59_out), .gate(1'b1));
  Transistor #(.\type ("n")) transistor_62 (.in(1'b0), .out(transistor_62_out), .gate(1'b1));
  Transistor transistor_63 (.in(1'b1), .out(transistor_63_out), .gate(1'b0));
  Transistor transistor_64 (.in(transistor_63_out), .out(transistor_49_out), .gate(1'b1));
  Transistor #(.\type ("n")) transistor_65 (.in(1'b0), .out(transistor_49_out), .gate(1'b1));
  Transistor transistor_66 (.in(1'b1), .out(transistor_66_out), .gate(1'b1));
  Transistor transistor_67 (.in(transistor_66_out), .out(transistor_50_out), .gate(1'b1));
  Transistor #(.\type ("n")) transistor_68 (.in(1'b0), .out(transistor_50_out), .gate(1'b1));
  Transistor transistor_69 (.in(1'b1), .out(transistor_69_out), .gate(1'b0));
  Transistor #(.\type ("n")) transistor_70 (.in(1'b0), .out(transistor_69_out), .gate(1'b0));
  Transistor transistor_71 (.in(1'b1), .out(transistor_71_out), .gate(1'b1));
  Transistor #(.\type ("n")) transistor_72 (.in(1'b0), .out(transistor_71_out), .gate(1'b1));
  Transistor transistor_73 (.in(1'b1), .out(output0_nand_C2), .gate(transistor_55_out));
  Transistor #(.\type ("n")) transistor_74 (.in(transistor_75_out), .out(output0_nand_C2), .gate(transistor_55_out));
  Transistor #(.\type ("n")) transistor_75 (.in(1'b0), .out(transistor_75_out), .gate(1'b0));
  Transistor transistor_76 (.in(1'b1), .out(output0_nand_C3), .gate(transistor_59_out));
  Transistor #(.\type ("n")) transistor_77 (.in(transistor_78_out), .out(output0_nand_C3), .gate(transistor_59_out));
  Transistor #(.\type ("n")) transistor_78 (.in(1'b0), .out(transistor_78_out), .gate(1'b1));
  Transistor transistor_79 (.in(1'b1), .out(transistor_79_out), .gate(1'b0));
  Transistor transistor_80 (.in(transistor_79_out), .out(output0_nor_C2), .gate(transistor_49_out));
  Transistor #(.\type ("n")) transistor_81 (.in(1'b0), .out(output0_nor_C2), .gate(transistor_49_out));
  Transistor transistor_82 (.in(1'b1), .out(transistor_82_out), .gate(1'b1));
  Transistor transistor_83 (.in(transistor_82_out), .out(output0_nor_C3), .gate(transistor_50_out));
  Transistor #(.\type ("n")) transistor_84 (.in(1'b0), .out(output0_nor_C3), .gate(transistor_50_out));
  Transistor transistor_85 (.in(1'b1), .out(transistor_85_out), .gate(transistor_69_out));
  Transistor transistor_86 (.in(transistor_85_out), .out(output0_not_C2), .gate(1'b1));
  Transistor #(.\type ("n")) transistor_87 (.in(transistor_88_out), .out(output0_not_C2), .gate(1'b1));
  Transistor #(.\type ("n")) transistor_88 (.in(1'b0), .out(transistor_88_out), .gate(1'b0));
  Transistor transistor_89 (.in(1'b1), .out(transistor_89_out), .gate(transistor_71_out));
  Transistor transistor_90 (.in(transistor_89_out), .out(output0_not_C3), .gate(1'b1));
  Transistor #(.\type ("n")) transistor_91 (.in(transistor_92_out), .out(output0_not_C3), .gate(1'b1));
  Transistor #(.\type ("n")) transistor_92 (.in(1'b0), .out(transistor_92_out), .gate(1'b1));
  Transistor transistor_93 (.in(1'b1), .out(output0_tg_C2), .gate(transistor_51_out));
  Transistor #(.\type ("n")) transistor_94 (.in(1'b1), .out(output0_tg_C2), .gate(1'b0));
  Transistor transistor_95 (.in(1'b1), .out(output0_tg_C3), .gate(transistor_53_out));
  Transistor #(.\type ("n")) transistor_96 (.in(1'b1), .out(output0_tg_C3), .gate(1'b1));

  // Notes on the sheet:
  //   input0_nand
  //   control_nand
  //   input0_nand
  //   control_nand
  //   Control with NAND gate
  //   Control with NOR gate
  //   input0_nor
  //   control_nor
  //   input0_nor
  //   control_nor
  //   Control with NOT gate
  //   input0_not
  //   control_not
  //   input0_not
  //   control_not
  //   input0_tg
  //   control_tg
  //   input0_tg
  //   control_tg
  //   Control with Transmission gate
  //   input0_nand
  //   control_nand
  //   input0_nand
  //   control_nand
  //   input0_nor
  //   control_nor
  //   input0_nor
  //   control_nor
  //   input0_not
  //   control_not
  //   input0_not
  //   control_not
  //   input0_tg
  //   control_tg
  //   input0_tg
  //   control_tg
endmodule
