// Logisim project XNOR gate all cases.circ as structural Verilog: 1 circuit, main circuit main
module main (
  output output0_C0,
  output output0_C2,
  output output0_C1,
  output output0_C3
);

  wire transistor_1_out, transistor_5_out, transistor_9_out, transistor_11_out, transistor_17_out,
       transistor_21_out, transistor_25_out, transistor_27_out;

  Transistor transistor_1 (.in(1'b0), .out(transistor_1_out), .gate(1'b0));
  Transistor transistor_2 (.in(1'b0), .out(transistor_1_out), .gate(1'b0));
  Transistor #(.\type ("n")) transistor_3 (.in(transistor_9_out), .out(transistor_1_out), .gate(1'b0));
  Transistor #(.\type ("n")) transistor_4 (.in(1'b0), .out(transistor_1_out), .gate(transistor_9_out));
  Transistor transistor_5 (.in(1'b0), .out(transistor_5_out), .gate(1'b1));
  Transistor transistor_6 (.in(1'b1), .out(transistor_5_out), .gate(1'b0));
  Transistor #(.\type ("n")) transistor_7 (.in(transistor_11_out), .out(transistor_5_out), .gate(1'b1));
  Transistor #(.\type ("n")) transistor_8 (.in(1'b1), .out(transistor_5_out), .gate(transistor_11_out));
  Transistor transistor_9 (.in(1'b1), .out(transistor_9_out), .gate(1'b0));
  Transistor #(.\type ("n")) transistor_10 (.in(1'b0), .out(transistor_9_out), .gate(1'b0));
  Transistor transistor_11 (.in(1'b1), .out(transistor_11_out), .gate(1'b0));
  Transistor #(.\type ("n")) transistor_12 (.in(1'b0), .out(transistor_11_out), .gate(1'b0));
  Transistor transistor_13 (.in(1'b1), .out(output0_C0), .gate(transistor_1_out));
  Transistor #(.\type ("n")) transistor_14 (.in(1'b0), .out(output0_C0), .gate(transistor_1_out));
  Transistor transistor_15 (.in(1'b1), .out(output0_C1), .gate(transistor_5_out));
  Transistor #(.\type ("n")) transistor_16 (.in(1'b0), .out(output0_C1), .gate(transistor_5_out));
  Transistor transistor_17 (.in(1'b1), .out(transistor_17_out), .gate(1'b0));
  Transistor transistor_18 (.in(1'b0), .out(transistor_17_out), .gate(1'b1));
  Transistor #(.\type ("n")) transistor_19 (.in(transistor_25_out), .out(transistor_17_out), .gate(1'b0));
  Transistor #(.\type ("n")) transistor_20 (.in(1'b0), .out(transistor_17_out), .gate(transistor_25_out));
  Transistor transistor_21 (.in(1'b1), .out(transistor_21_out), .gate(1'b1));
  Transistor transistor_22 (.in(1'b1), .out(transistor_21_out), .gate(1'b1));
  Transistor #(.\type ("n")) transistor_23 (.in(transistor_27_out), .out(transistor_21_out), .gate(1'b1));
  Transistor #(.\type ("n")) transistor_24 (.in(1'b1), .out(transistor_21_out), .gate(transistor_27_out));
  Transistor transistor_25 (.in(1'b1), .out(transistor_25_out), .gate(1'b1));
  Transistor #(.\type ("n")) transistor_26 (.in(1'b0), .out(transistor_25_out), .gate(1'b1));
  Transistor transistor_27 (.in(1'b1), .out(transistor_27_out), .gate(1'b1));
  Transistor #(.\type ("n")) transistor_28 (.in(1'b0), .out(transistor_27_out), .gate(1'b1));
  Transistor transistor_29 (.in(1'b1), .out(output0_C2), .gate(transistor_17_out));
  Transistor #(.\type ("n")) transistor_30 (.in(1'b0), .out(output0_C2), .gate(transistor_17_out));
  Transistor transistor_31 (.in(1'b1), .out(output0_C3), .gate(transistor_21_out));
  Transistor #(.\type ("n")) transistor_32 (.in(1'b0), .out(output0_C3), .gate(transistor_21_out));

  // Notes on the sheet:
  //   input0
  //   input1
  //   input0
  //   input1
  //   input0
  //   input1
  //   input0
  //   input1
endmodule
