// Logisim project XOR gate all cases.circ as structural Verilog: 1 circuit, main circuit main
module main (
  output output0_C0,
  output output0_C2,
  output output0_C1,
  output output0_C3
);

  wire transistor_9_out, transistor_11_out, transistor_21_out, transistor_23_out;

  Transistor transistor_1 (.in(1'b0), .out(output0_C0), .gate(1'b0));
  Transistor transistor_2 (.in(1'b0), .out(output0_C0), .gate(1'b0));
  Transistor #(.\type ("n")) transistor_3 (.in(transistor_9_out), .out(output0_C0), .gate(1'b0));
  Transistor #(.\type ("n")) transistor_4 (.in(1'b0), .out(output0_C0), .gate(transistor_9_out));
  Transistor transistor_5 (.in(1'b0), .out(output0_C1), .gate(1'b1));
  Transistor transistor_6 (.in(1'b1), .out(output0_C1), .gate(1'b0));
  Transistor #(.\type ("n")) transistor_7 (.in(transistor_11_out), .out(output0_C1), .gate(1'b1));
  Transistor #(.\type ("n")) transistor_8 (.in(1'b1), .out(output0_C1), .gate(transistor_11_out));
  Transistor transistor_9 (.in(1'b1), .out(transistor_9_out), .gate(1'b0));
  Transistor #(.\type ("n")) transistor_10 (.in(1'b0), .out(transistor_9_out), .gate(1'b0));
  Transistor transistor_11 (.in(1'b1), .out(transistor_11_out), .gate(1'b0));
  Transistor #(.\type ("n")) transistor_12 (.in(1'b0), .out(transistor_11_out), .gate(1'b0));
  Transistor transistor_13 (.in(1'b1), .out(output0_C2), .gate(1'b0));
  Transistor transistor_14 (.in(1'b0), .out(output0_C2), .gate(1'b1));
  Transistor #(.\type ("n")) transistor_15 (.in(transistor_21_out), .out(output0_C2), .gate(1'b0));
  Transistor #(.\type ("n")) transistor_16 (.in(1'b0), .out(output0_C2), .gate(transistor_21_out));
  Transistor transistor_17 (.in(1'b1), .out(output0_C3), .gate(1'b1));
  Transistor transistor_18 (.in(1'b1), .out(output0_C3), .gate(1'b1));
  Transistor #(.\type ("n")) transistor_19 (.in(transistor_23_out), .out(output0_C3), .gate(1'b1));
  Transistor #(.\type ("n")) transistor_20 (.in(1'b1), .out(output0_C3), .gate(transistor_23_out));
  Transistor transistor_21 (.in(1'b1), .out(transistor_21_out), .gate(1'b1));
  Transistor #(.\type ("n")) transistor_22 (.in(1'b0), .out(transistor_21_out), .gate(1'b1));
  Transistor transistor_23 (.in(1'b1), .out(transistor_23_out), .gate(1'b1));
  Transistor #(.\type ("n")) transistor_24 (.in(1'b0), .out(transistor_23_out), .gate(1'b1));

  // Notes on the sheet:
  //   input0
  //   input1
  //   input0
  //   input1
  //   input0
  //   input1
  //   input0
  //   input1
endmodule
